# Fritzing sketch verkeerslicht_sketch (saved by Fritzing 0.9.3b)
breadboards: 1

parts:
  Onderdeel1 = Arduino Uno (Rev3)
  LED1 = LED - 5mm [color="Red (633nm)" package="5 mm [THT]"]
  LED2 = LED - 5mm [color="Orange (605nm)" package="5 mm [THT]"]
  LED3 = LED - 5mm [color="Green (555nm)" package="5 mm [THT]"]
  R1 = Resistor [tolerance=±5% resistance=220 package=THT]
  R2 = Resistor [tolerance=±5% resistance=220 package=THT]
  R3 = Resistor [tolerance=±5% resistance=220 package=THT]

nets:
  N1: Onderdeel1.D8, LED1.cathode
  N2: Onderdeel1.D9_PWM, LED2.cathode
  N3: Onderdeel1.D10_PWM/SS, LED3.cathode
  N4: Onderdeel1.GND, R1.Pin_0, R2.Pin_0, R3.Pin_0
  N5: LED1.anode, R1.Pin_1
  N6: LED2.anode, R2.Pin_1
  N7: LED3.anode, R3.Pin_1
